# Fritzing sketch breadboard (saved by Fritzing 0.9.6b)
breadboards: 1

parts:
  Part3 = Adafruit DRV8871 [part_number="Adafruit #3190"]  # not connected
  Adafruit_ADS7830_8-Channel_8-Bit_ADC1 = Adafruit ADS7830 8-Channel 8-Bit ADC [part_number=#5836]
  Mod1 = Raspberry Pi 4B
  Part4 = Soil Moisture Sensor
  Part5 = Soil Moisture Sensor
  Part6 = Soil Moisture Sensor
  Part7 = Soil Moisture Sensor
  AM1 = AM2302 Humidity and Temperature Sensor

nets:
  N1: Adafruit_ADS7830_8-Channel_8-Bit_ADC1.A0, Part4.SIG
  N2: Adafruit_ADS7830_8-Channel_8-Bit_ADC1.A1, Part5.SIG
  N3: Adafruit_ADS7830_8-Channel_8-Bit_ADC1.A2, Part6.SIG
  N4: Adafruit_ADS7830_8-Channel_8-Bit_ADC1.A3, Part7.SIG
  VCC: Adafruit_ADS7830_8-Channel_8-Bit_ADC1.VCC, Part4.VCC, Part5.VCC, Part6.VCC, Part7.VCC, AM1.VDD
  GND: Adafruit_ADS7830_8-Channel_8-Bit_ADC1.GND, Part4.GND, Part5.GND, Part6.GND, Part7.GND, AM1.GND
  N5: Adafruit_ADS7830_8-Channel_8-Bit_ADC1.SCL, Mod1.GPIO3
  N6: Adafruit_ADS7830_8-Channel_8-Bit_ADC1.SDA, Mod1.GPIO2
  N7: Mod1.GPIO15, AM1.DATA

custom parts:
  Adafruit DRV8871: Crank up your robotics with powerful Adafruit DRV8871 motor driver breakout board. This motor driver has a lot of great specs that make it useful for a wide variety of mechatronics. In particular, the simple resistor-set current limiting and auto-magic PWM support make it super easy to use. Check out the specs for the DRV8871: 6.5V to 45V motor power voltage Up to 5.5V logic level on IN pins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
  Adafruit ADS7830 8-Channel 8-Bit ADC: Many microcontrollers have ADCs these days, for reading analog/resistive sensors like potentiometers, thermistors, LDR light sensors, etc. but sometimes you need MOAR! Or maybe you're using a single board computer like a Raspberry Pi that has no ADCs at all! The Adafruit ADS7830 8-Channel 8-Bit ADC with I2C is an affordable 8-channel ADC with I2C interface, so it's easy to include with any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
